# Fritzing sketch Rilees Birthday Box (saved by Fritzing 1.0.3b)
circuit board: 9.99242cm x 7.03024cm

parts:
  Part1 = Arduino Nano (Rev3.0)
  R1 = TRIMPOT [maximum_resistance=10kΩ knob_status=50% power=0.5W package=3362u-2]
  S1 = Toggle Switch spst [package=THT]
  microSD1 = MicroSD Card Module
  SPKR1 = Loudspeaker
  J1 = Piezo Speaker
  C1 = Capacitor [package=cap-pth-large]
  C2 = Capacitor [package=cap-pth-large]
  C3 = Capacitor [package=cap-pth-large]
  C4 = Capacitor [package=cap-pth-large]
  Q1 = npn-Powertransistor [package="TO220 [THT]"]
  R5 = Resistor [tolerance=±5% power=0.25W resistance=220 package=THT]
  I2C1 = OLED 128x64 I2C Monochrome Display
  R6 = Resistor [tolerance=±5% power=0.25W resistance=220 package=THT]
  R7 = Resistor [tolerance=±5% power=0.25W resistance=220 package=THT]
  R8 = Resistor [tolerance=±5% power=0.25W resistance=220 package=THT]
  RE1 = Rotary Encoder [package=THT]
  BAT1 = BC9VPC [package=bc9vpc]
  R9 = Resistor [tolerance=±5% power=0.25W resistance=220 package=THT]

nets:
  GND: Part1.GND, microSD1.GND, J1.pin1, C1.1, C2.1, C3.1, Q1.emitter, R5.Pin_0, I2C1.GND, RE1.EncoderPinC, RE1.SwitchPinE, BAT1.V-, R9.Pin_1
  N1: Part1.D2, C1.2, R6.Pin_0, RE1.EncoderPinA
  N2: Part1.D3, C2.2, R7.Pin_0, RE1.EncoderPinB
  N3: Part1.D4, C3.2, R8.Pin_0, RE1.SwitchrPinD
  N4: Part1.D8, J1.pin2, R5.Pin_1
  N5: Part1.D9, C4.1
  N6: Part1.D10, microSD1.CS
  N7: Part1.D11/MOSI, microSD1.MOSI
  N8: Part1.D12/MISO, microSD1.MISO
  N9: Part1.VIN, S1.L1, SPKR1.pin2
  5V: Part1.5V, microSD1.VCC, I2C1.VDD, R6.Pin_1, R7.Pin_1, R8.Pin_1
  N10: Part1.A5, I2C1.SCK
  N11: Part1.A4, I2C1.SDA
  N12: Part1.D13/SCK, microSD1.SCK
  N13: R1.CCW, R9.Pin_0
  N14: R1.WIPER, C4.2, Q1.base
  N15: R1.CW, SPKR1.pin1, Q1.collector
  N16: S1.COM, BAT1.V+

custom parts:
  Toggle Switch spst: Toggle Switch single pole single throw
  Rotary Encoder: Rotary Encoder from ALPSec11e with switch.
