# Fritzing sketch DnD Terminal Fritzing (saved by Fritzing 1.0.3b)
circuit board: 10.0214cm x 6.94971cm
breadboards: 1

parts:
  NANO_EVERY = Arduino Nano Every THT
  OLED1 = OLED 128x64 I2C Monochrome Display
  SW1 = Taiway 100-SP-X-T1 SPDT Miniature Toggle Switch [part_number=100-SP-X-T1-0-0-B1-M1 package=THT]
  R1 = Resistor [tolerance=±5% power=0.25W resistance=220 package=THT]
  BUT1 = YXQ 1x5 membrane keypad
  R2 = Resistor [tolerance=±5% power=0.25W resistance=220 package=THT]
  R3 = Resistor [tolerance=±5% power=0.25W resistance=220 package=THT]
  R4 = Resistor [tolerance=±5% power=0.25W resistance=220 package=THT]
  BAT1 = BC9VPC [package=bc9vpc]
  R5 = Resistor [tolerance=±5% power=0.25W resistance=220 package=THT]
  BUT2 = Round Pushbutton
  R6 = Resistor [tolerance=±5% power=0.25W resistance=220 package=THT]
  J1 = Piezo Speaker
  R7 = Resistor [tolerance=±5% power=0.25W resistance=220 package=THT]

nets:
  N1: NANO_EVERY.Pin_4, J1.pin2, R7.Pin_0
  N2: NANO_EVERY.Pin_6, BUT2.leg1, R6.Pin_0
  N3: NANO_EVERY.Pin_7, BUT1.Pin_1, R5.Pin_0
  N4: NANO_EVERY.Pin_8, BUT1.Pin_2, R4.Pin_0
  N5: NANO_EVERY.Pin_9, BUT1.Pin_3, R3.Pin_0
  N6: NANO_EVERY.Pin_10, BUT1.Pin_4, R2.Pin_0
  N7: NANO_EVERY.Pin_11, R1.Pin_0, BUT1.Pin_5
  N8: NANO_EVERY.Pin_12, BUT1.Pin_6, BAT1.V-, BUT2.leg0, J1.pin1, R7.Pin_1
  N9: NANO_EVERY.Pin_13, NANO_EVERY.Pin_18
  N10: NANO_EVERY.Pin_14, NANO_EVERY.Pin_19, OLED1.VDD, R1.Pin_1, R2.Pin_1, R3.Pin_1, R4.Pin_1, R5.Pin_1, R6.Pin_1
  N11: NANO_EVERY.Pin_16, SW1.COM
  N12: NANO_EVERY.Pin_17, OLED1.GND
  N13: NANO_EVERY.Pin_22, OLED1.SCK
  N14: NANO_EVERY.Pin_23, OLED1.SDA
  N15: SW1.L2, BAT1.V+

custom parts:
  Arduino Nano Every THT: The Nano Every is Arduino’s 5V compatible board in the smallest available form factor: 45x18mm! The Arduino Nano is the preferred board for many projects requiring a small and easy to use microcontroller board. The small footprint and low price, make the Nano Every particularly suited for wearable inventions, low cost robotics, electronic musical instruments, and general use to control smaller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
  YXQ 1x5 membrane keypad: Membrane Switch;Key Type : 1x5;Voltage : DC 12V.
