# Fritzing sketch ESET 349 Project PCB (saved by Fritzing 1.0.3b)
breadboards: 1

parts:
  Mod1 = MSP-EXP432P401R_EagleCAD
  R1 = Resistor [tolerance=±5% power=0.25W resistance=220 package=THT]
  R2 = Resistor [tolerance=±5% power=0.25W resistance=220 package=THT]
  R3 = Resistor [tolerance=±5% power=0.25W resistance=220 package=THT]
  R4 = Resistor [tolerance=±5% power=0.25W resistance=220 package=THT]
  R5 = Resistor [tolerance=±5% power=0.25W resistance=220 package=THT]
  R6 = Resistor [tolerance=±5% power=0.25W resistance=220 package=THT]
  R7 = Resistor [tolerance=±5% power=0.25W resistance=220 package=THT]
  R8 = Resistor [tolerance=±5% power=0.25W resistance=220 package=THT]
  R9 = Resistor [tolerance=±5% power=0.25W resistance=220 package=THT]
  R10 = Resistor [tolerance=±5% power=0.25W resistance=220 package=THT]
  LED1 = LED - 5mm [color="Red (633nm)" current=0.030A package="5 mm [THT]"]
  LED2 = LED - 5mm [color="Red (633nm)" current=0.030A package="5 mm [THT]"]
  S1 = Pushbutton [package="[THT]"]
  S2 = Pushbutton [package="[THT]"]
  S3 = Pushbutton [package="[THT]"]
  S4 = Pushbutton [package="[THT]"]
  S5 = Pushbutton [package="[THT]"]
  LED3 = LED - 5mm [color="Red (633nm)" current=0.030A package="5 mm [THT]"]
  LED4 = LED - 5mm [color="Red (633nm)" current=0.030A package="5 mm [THT]"]
  LED5 = LED - 5mm [color="Red (633nm)" current=0.030A package="5 mm [THT]"]
  S6 = Pushbutton [package="[THT]"]
  J1 = Piezo Speaker
  R11 = Resistor [tolerance=±5% power=0.25W resistance=220 package=THT]
  R12 = Resistor [tolerance=±5% power=0.25W resistance=220 package=THT]

nets:
  N1: Mod1.P4.1, Mod1.P4.3, R2.Pin_1, S2.Pin_3, S2.Pin_4
  N2: Mod1.P4.6, S6.Pin_3, S6.Pin_4, R12.Pin_1
  N3: Mod1.5V, Mod1.DEBUG_P_5V, R1.Pin_0, R2.Pin_0, R3.Pin_0, R4.Pin_0, R5.Pin_0, S1.Pin_1, S1.Pin_2, S2.Pin_1, S2.Pin_2, S3.Pin_1, S3.Pin_2, S4.Pin_1, S4.Pin_2, S5.Pin_1, S5.Pin_2, S6.Pin_1, S6.Pin_2, R12.Pin_0
  N4: Mod1.GND, R6.Pin_1, R7.Pin_1, R8.Pin_1, R9.Pin_1, R10.Pin_1, J1.pin1, R11.Pin_1
  N5: Mod1.P4.0, R1.Pin_1, S1.Pin_3, S1.Pin_4
  N6: Mod1.P4.2, Mod1.P4.4, R3.Pin_1, R4.Pin_1, S3.Pin_3, S3.Pin_4, S4.Pin_3, S4.Pin_4
  N7: Mod1.P4.5, R5.Pin_1, S5.Pin_3, S5.Pin_4
  N8: Mod1.P5.4, LED2.anode
  N9: Mod1.P5.5, LED1.anode
  N10: Mod1.P2.4, J1.pin2, R11.Pin_0
  N11: Mod1.P5.1, Mod1.P3.5, LED4.anode
  N12: Mod1.P5.0, LED5.anode
  N13: Mod1.P5.2, Mod1.P5.6, LED3.anode
  N14: R6.Pin_0, LED5.cathode
  N15: R7.Pin_0, LED4.cathode
  N16: R8.Pin_0, LED3.cathode
  N17: R9.Pin_0, LED2.cathode
  N18: R10.Pin_0, LED1.cathode

custom parts:
  MSP-EXP432P401R_EagleCAD: TI Launch pad MSP-EXP432P401R development board.
